// Logisim project alu.circ as structural Verilog: 2 circuits, main circuit alu
module alu (
  input  [31:0] A,
  input  [31:0] B,
  input  [3:0] ALUSel,
  output [31:0] Result,
  output out_5,
  output out_6,
  output out_7,
  output out_8
);

  wire comparator_1_lt, qf_3_jw;
  wire [31:0] A1, add0, adder_2_out, and0, B1, bit_extender_2_out, divider_2_out, divu0, mul0, mulh0, mulhu0,
       multiplier_1_out, multiplier_4_cout, multiplier_4_out, not_1_out, or0, qf_1_val, qf_2_val, remu0,
       sll0, slt0, sra0, srl0, sub0, xor0;

  Multiplexer #(.width(32), .enable("false")) multiplexer_1 (.in0(A), .in1(qf_1_val), .out(A1), .sel(A[31]));
  qf qf_1 (.A(A), .VAL(qf_1_val));  // open: jw
  qf qf_2 (.A(B), .VAL(qf_2_val));  // open: jw
  xor xor_1 (out_5, A[31], B[31]);
  Multiplexer #(.width(32), .enable("false")) multiplexer_2 (.in0(B), .in1(qf_2_val), .out(B1), .sel(B[31]));
  Shifter #(.width(32), .shift("lr")) shifter_1 (.in(A), .\dist (B[4:0]), .out(srl0));
  Shifter #(.width(32), .shift("ar")) shifter_2 (.in(A), .\dist (B[4:0]), .out(sra0));
  Shifter #(.width(32)) shifter_3 (.in(A), .\dist (B[4:0]), .out(sll0));
  Adder #(.width(32)) adder_1 (.a(A), .b(B), .out(add0));  // open: cin, cout
  assign and0 = A & B;  // AND_Gate and_1, 32 bits wide
  assign or0 = A | B;  // OR_Gate or_1, 32 bits wide
  assign xor0 = A ^ B;  // XOR_Gate xor_2, 32 bits wide
  Comparator #(.width(32)) comparator_1 (.a(A), .b(B), .lt(comparator_1_lt));  // open: gt, eq
  Divider #(.width(32)) divider_1 (.a(A), .b(B), .out(divu0));  // open: upper, rem
  Divider #(.width(32)) divider_2 (.a(A), .b(B), .out(divider_2_out));  // open: upper, rem
  assign slt0 = {{31{1'b0}}, comparator_1_lt};  // Bit_Extender bit_extender_1
  Multiplier #(.width(32)) multiplier_1 (.a(divider_2_out), .b(B), .out(multiplier_1_out));  // open: cin, cout
  Subtractor #(.width(32)) subtractor_1 (.a(A), .b(multiplier_1_out), .out(remu0));  // open: bin, bout
  Multiplier #(.width(32)) multiplier_2 (.a(A), .b(B), .cout(mulhu0));  // open: out, cin
  Multiplier #(.width(32)) multiplier_3 (.a(A), .b(B), .out(mul0));  // open: cin, cout
  Subtractor #(.width(32)) subtractor_2 (.a(A), .b(B), .out(sub0));  // open: bin, bout
  Multiplier #(.width(32)) multiplier_4 (
    .a(A1), .b(B1), .out(multiplier_4_out), .cout(multiplier_4_cout));  // open: cin
  Multiplexer #(.select(4), .width(32), .enable("false")) multiplexer_3 (
    .in0(add0), .in1(and0), .in2(or0), .in3(xor0), .in4(srl0), .in5(sra0), .in6(sll0), .in7(slt0),
    .in8(divu0), .in9(remu0), .in10(mul0), .in11(mulhu0), .in12(sub0), .in13(B), .in14(mulh0), .out(Result),
    .sel(ALUSel));  // open: in15
  assign not_1_out = ~multiplier_4_cout;  // NOT_Gate not_1, 32 bits wide
  qf qf_3 (.A(multiplier_4_out), .jw(qf_3_jw));  // open: VAL
  Multiplexer #(.width(32), .enable("false")) multiplexer_4 (
    .in0(multiplier_4_cout), .in1(adder_2_out), .out(mulh0), .sel(out_5));
  assign bit_extender_2_out = {{31{1'b0}}, qf_3_jw};  // Bit_Extender bit_extender_2
  Adder #(.width(32)) adder_2 (.a(not_1_out), .b(bit_extender_2_out), .out(adder_2_out));  // open: cin, cout

  assign out_6 = B[31];
  assign out_7 = A[31];
  assign out_8 = A[31];

  // Other names for the same wires on the sheet: AS = A[31]; BS = B[31]; VS = out_5

  // Notes on the sheet:
  //   INPUTS to your circuit
  //   DON'T CHANGE THE LOCATIONS OF THE INPUTS AND OUTPUTS!
  //   OUTPUT from your circuit
endmodule

module qf (
  input  [31:0] A,
  output [31:0] VAL,
  output jw
);

  wire [31:0] not_1_out;

  assign not_1_out = ~A;  // NOT_Gate not_1, 32 bits wide
  Adder #(.width(32)) adder_1 (.a(not_1_out), .b(32'h1), .out(VAL), .cout(jw));  // open: cin
endmodule
