// Logisim project cpu.circ as structural Verilog: 19 circuits, main circuit main
module main (
  input  [31:0] INSTRUCTION,
  input  CLOCK,
  output [31:0] PROGRAM_COUNTER,
  output [31:0] ra,
  output [31:0] sp,
  output [31:0] t0,
  output [31:0] t1,
  output [31:0] t2,
  output [31:0] s0,
  output [31:0] s1,
  output [31:0] a0
);

  wire Asel, Breq, Brlt, bsel, control_1_regw, DMEM_p1, DMEM_p6, memrw, pcsel, regw;
  wire [1:0] wbsel;
  wire [2:0] func3, isetmath_1_alusel;
  wire [3:0] Balu, Ialu, multiplexer_5_out, rsetmath_1_alusel;
  wire [4:0] immsw, rs1, rs2;
  wire [6:0] func7or115, opcode;
  wire [11:0] imm;
  wire [31:0] ALU, DMEM_p8, Iimm, immR, INSTRUCTION1, load_1_dataout, multiplexer_1_out, multiplexer_2_out,
       multiplexer_3_out, multiplexer_4_out, multiplexer_6_out, Pc4, register_1_q, rs1r, rs2r, SBimm, Simm,
       Uimm, UJimm1;

  Multiplexer #(.width(32), .enable("false")) multiplexer_1 (
    .in0(Pc4), .in1(ALU), .out(multiplexer_1_out), .sel(pcsel));
  // Probe on INSTRUCTION1
  Adder #(.width(32)) adder_1 (.a(PROGRAM_COUNTER), .b(32'h4), .out(Pc4));  // open: cin, cout
  Pcsel pcsel_1 (.opcode(opcode), .func3(func3), .Breq(Breq), .Brlt(Brlt), .Pcsel(pcsel));
  Register #(.width(32)) PC (.D(multiplexer_1_out), .en(1'b1), .clk(CLOCK), .Q(PROGRAM_COUNTER));  // open: clr
  asel1 asel1_1 (.opcode(opcode), .Asel(Asel));
  Register #(.width(32)) register_1 (.D(PROGRAM_COUNTER), .en(1'b1), .clk(CLOCK), .Q(register_1_q));  // open: clr
  instsplit instsplit_1 (
    .inst(INSTRUCTION1), .opcode(opcode), .rdorimm40(immsw), .func3(func3), .rs1(rs1), .rs2(rs2),
    .func7orimm115(func7or115), .imm12(imm));
  Multiplexer #(.width(32), .enable("false")) multiplexer_2 (
    .in0(INSTRUCTION), .in1(32'h13), .out(multiplexer_2_out), .sel(pcsel));
  Register #(.width(32)) register_2 (.D(multiplexer_2_out), .en(1'b1), .clk(CLOCK), .Q(INSTRUCTION1));  // open: clr
  immchoose immchoose_1 (
    .opcode(opcode), .Iimm(Iimm), .Simm(Simm), .SBimm(SBimm), .UJimm(UJimm1), .Uimm(Uimm), .imm(immR));
  RegWEn regwen_1 (.opcode(opcode), .regw(regw));
  // Probe on rs1
  // Probe on rs2
  // Probe on immsw
  assign Simm = {{20{func7or115[6]}}, {func7or115, immsw}};  // Bit_Extender bit_extender_1
  // Probe on immR
  alucontrol alucontrol_1 (.Ialu(Ialu), .opcode(opcode), .Balu(Balu));
  Isetmath isetmath_1 (.Opcode4(opcode[4]), .func3(func3), .imm(imm), .alusel(isetmath_1_alusel), .immout(Iimm));
  Rsetmath rsetmath_1 (.func3(func3), .func7(func7or115), .alusel(rsetmath_1_alusel));
  control control_1 (
    .opcode4(opcode[4]), .opcode5(opcode[5]), .opcode2(opcode[2]), .regw(control_1_regw), .memrw(memrw),
    .bsel(bsel));  // open: wbsel
  Sbsetmath sbsetmath_1 (.func7orimm(func7or115), .rdorimm5(immsw), .SBimm(SBimm));
  Uimm Uimm1 (.instruction1(INSTRUCTION1), .Uimm(Uimm));
  UJimm u_Ujimm1 (.Instruction1(INSTRUCTION1), .UJimm1(UJimm1));
  regfile_main RegFile (
    .rs2(rs2), .rd(immsw), .Read_Data_1(rs1r), .Read_Data_2(rs2r), .ra(ra), .sp(sp), .t0(t0), .t1(t1),
    .t2(t2), .s0(s0), .s1(s1), .a0(a0), .rs1(rs1), .Write_Data(multiplexer_6_out), .RegWEn(regw), .clk(CLOCK));  // open: out_17
  // Probe on rs2r
  assign Ialu = {{1{1'b0}}, isetmath_1_alusel};  // Bit_Extender bit_extender_2
  // Probe on rs1r
  // Probe on multiplexer_6_out
  Multiplexer #(.width(32), .enable("false")) multiplexer_3 (
    .in0(rs1r), .in1(register_1_q), .out(multiplexer_3_out), .sel(Asel));
  Multiplexer #(.width(32), .enable("false")) multiplexer_4 (
    .in0(rs2r), .in1(immR), .out(multiplexer_4_out), .sel(bsel));
  Multiplexer #(.width(4), .enable("false")) multiplexer_5 (
    .in0(rsetmath_1_alusel), .in1(Balu), .out(multiplexer_5_out), .sel(bsel));
  alu Arithmetic_Logic_Unit (
    .B(multiplexer_4_out), .Result(ALU), .A(multiplexer_3_out), .ALUSel(multiplexer_5_out));  // open: out_7, out_5, out_6, out_8
  wbsel1 wbsel1_1 (.opcode(opcode), .wbsel(wbsel));
  Multiplexer #(.select(2), .width(32), .enable("false")) multiplexer_6 (
    .in0(load_1_dataout), .in1(ALU), .in2(PROGRAM_COUNTER), .out(multiplexer_6_out), .sel(wbsel));  // open: in3
  // Probe on wbsel
  // Probe on ALU
  // Probe on ALU
  Branchcomp branchcomp_1 (.rs1(rs1r), .rs2(rs2r), .func3(func3), .Breq(Breq), .Brlt(Brlt));
  // mem_main DMEM: pin names not known; wires that end beside it: DMEM_p1, ALU, rs2r, DMEM_p1, CLOCK, DMEM_p6, memrw, DMEM_p8
  load load_1 (.address(ALU), .data(DMEM_p8), .func3(func3), .dataout(load_1_dataout));

  // Other names for the same wires on the sheet: clk = CLOCK; rd[4:0] = immsw; immsw[11:5] = func7or115

  // Notes on the sheet:
  //   Output
  //   IMEM (do **NOT** move this)
  //   Inputs
  //   Inputs/Outputs for testing. Do **NOT** move these.
endmodule

module Isetmath (
  input  Opcode4,
  input  [2:0] func3,
  input  [11:0] imm,
  output [2:0] alusel,
  output [31:0] immout
);

  wire and_1_out, comparator_1_eq;
  wire [2:0] multiplexer_1_out, multiplexer_2_out;

  Comparator #(.width(3)) comparator_1 (.a(3'b101), .b(func3), .eq(comparator_1_eq));  // open: gt, lt
  Multiplexer #(.width(3), .enable("false")) multiplexer_1 (
    .in0(func3), .in1(3'b011), .out(multiplexer_1_out), .sel(and_1_out));
  and and_1 (and_1_out, imm[10], comparator_1_eq);
  Multiplexer #(.select(3), .width(3), .enable("false")) multiplexer_2 (
    .in0(3'b000), .in1(3'b110), .in2(3'b111), .in3(3'b101), .in4(3'b011), .in5(3'b100), .in6(3'b010),
    .in7(3'b001), .out(multiplexer_2_out), .sel(multiplexer_1_out));
  Multiplexer #(.width(3), .enable("false")) multiplexer_3 (
    .in0(3'b000), .in1(multiplexer_2_out), .out(alusel), .sel(Opcode4));
  assign immout = {{20{imm[11]}}, imm};  // Bit_Extender bit_extender_1

  // Other names for the same wires on the sheet: sign = imm[10]
endmodule

module lwlhlb (
  input  opcode4,
  input  [11:0] imm,
  input  [2:0] func3,
  output [11:0] immout
);

  wire [11:0] multiplexer_1_out, shifter_1_out, shifter_2_out, shifter_3_out;

  Shifter #(.width(12), .shift("ar")) shifter_1 (.in(imm), .\dist (4'b0011), .out(shifter_1_out));
  Shifter #(.width(12), .shift("ar")) shifter_2 (.in(imm), .\dist (4'b0011), .out(shifter_2_out));
  Shifter #(.width(12), .shift("ar")) shifter_3 (.in(imm), .\dist (4'b0100), .out(shifter_3_out));
  Multiplexer #(.select(3), .width(12), .enable("false")) multiplexer_1 (
    .in0(shifter_1_out), .in1(shifter_2_out), .in2(shifter_3_out), .out(multiplexer_1_out), .sel(func3));  // open: in3, in4, in5, in6, in7
  Multiplexer #(.width(12), .enable("false")) multiplexer_2 (
    .in0(multiplexer_1_out), .in1(imm), .out(immout), .sel(opcode4));
endmodule

module instsplit (
  input  [31:0] inst,
  output [6:0] opcode,
  output [4:0] rdorimm40,
  output [2:0] func3,
  output [4:0] rs1,
  output [4:0] rs2,
  output [6:0] func7orimm115,
  output [11:0] imm12
);


  assign func3 = inst[14:12];
  assign func7orimm115 = inst[31:25];
  assign imm12 = inst[31:20];
  assign opcode = inst[6:0];
  assign rdorimm40 = inst[11:7];
  assign rs1 = inst[19:15];
  assign rs2 = inst[24:20];
endmodule

module Rsetmath (
  input  [2:0] func3,
  input  [6:0] func7,
  output [3:0] alusel
);

  wire [3:0] multiplexer_1_out;

  Multiplexer #(.select(4), .width(4), .enable("false")) multiplexer_1 (
    .in0(4'b0000), .in1(4'b0110), .in2(4'b0111), .in4(4'b0011), .in5(4'b0100), .in6(4'b0010), .in7(4'b0001),
    .in8(4'b1010), .in9(4'b1110), .in11(4'b1011), .in13(4'b1000), .in15(4'b1001), .out(multiplexer_1_out),
    .sel({func7[0], func3}));  // open: in3, in10, in12, in14
  Multiplexer #(.width(4), .enable("false")) multiplexer_2 (
    .in0(multiplexer_1_out), .in1(4'b1100), .out(alusel), .sel(func7[5]));
endmodule

module instype (
  input  opcode4,
  input  opcode5,
  output [1:0] itype
);

  Multiplexer #(.select(2), .width(2), .enable("false")) multiplexer_1 (
    .in0(2'b00), .in1(2'b01), .out(itype), .sel({opcode5, opcode4}));  // open: in2, in3
endmodule

module control (
  input  opcode4,
  input  opcode5,
  input  opcode2,
  output regw,
  output memrw,
  output bsel,
  output wbsel
);

  wire and_2_out, and_3_out, not_1_out, not_2_out, not_3_out;

  not not_1 (not_1_out, opcode2);
  not not_2 (not_2_out, opcode4);
  not not_3 (not_3_out, opcode5);
  and and_1 (memrw, not_2_out, opcode5);
  and and_2 (and_2_out, opcode4, not_1_out, opcode5);
  and and_3 (and_3_out, not_2_out, not_3_out);
  not not_4 (regw, memrw);
  not not_5 (bsel, and_2_out);
  not not_6 (wbsel, and_3_out);
endmodule

module memrw (
  input  opcode4,
  input  opcode5,
  output memrw
);

  wire not_1_out;

  not not_1 (not_1_out, opcode4);
  and and_1 (memrw, not_1_out, opcode5);
endmodule

module Branchcomp (
  input  [31:0] rs1,
  input  [31:0] rs2,
  input  [2:0] func3,
  output Breq,
  output Brlt
);

  wire comparator_1_eq, comparator_1_lt, comparator_2_eq, comparator_2_lt;

  Comparator #(.width(32)) comparator_1 (.a(rs1), .b(rs2), .eq(comparator_1_eq), .lt(comparator_1_lt));  // open: gt
  Comparator #(.width(32), .mode("unsigned")) comparator_2 (
    .a(rs1), .b(rs2), .eq(comparator_2_eq), .lt(comparator_2_lt));  // open: gt
  Multiplexer #(.enable("false")) multiplexer_1 (
    .in0(comparator_1_lt), .in1(comparator_2_lt), .out(Brlt), .sel(func3[1]));
  Multiplexer #(.enable("false")) multiplexer_2 (
    .in0(comparator_1_eq), .in1(comparator_2_eq), .out(Breq), .sel(func3[1]));

  // Other names for the same wires on the sheet: sign = func3[1]
endmodule

module Sbsetmath (
  input  [6:0] func7orimm,
  input  [4:0] rdorimm5,
  output [31:0] SBimm
);

  assign SBimm = {{19{func7orimm[6]}}, {func7orimm[6], rdorimm5[0], func7orimm[5:0], rdorimm5[4:1], 1'b0}};  // Bit_Extender bit_extender_1
endmodule

module immchoose (
  input  [6:0] opcode,
  input  [31:0] Iimm,
  input  [31:0] Simm,
  input  [31:0] SBimm,
  input  [31:0] UJimm,
  input  [31:0] Uimm,
  output [31:0] imm
);

  wire and_1_out, and_2_out, not_1_out, not_2_out, or_1_out, or_2_out;
  wire [1:0] and_4_out;
  wire [31:0] multiplexer_1_out;

  not not_1 (not_1_out, opcode[3]);
  not not_2 (not_2_out, opcode[2]);
  and and_1 (and_1_out, not_1_out, opcode[5]);
  Multiplexer #(.width(32), .enable("false")) multiplexer_1 (
    .in0(Simm), .in1(SBimm), .out(multiplexer_1_out), .sel(opcode[6]));
  and and_2 (and_2_out, opcode[5], opcode[2]);
  or or_1 (or_1_out, opcode[3], opcode[4]);
  or or_2 (or_2_out, not_2_out, opcode[4]);
  and and_3 (and_4_out[1], and_2_out, or_1_out);
  and and_4 (and_4_out[0], or_2_out, and_1_out);
  Multiplexer #(.select(2), .width(32), .enable("false")) multiplexer_2 (
    .in0(Iimm), .in1(multiplexer_1_out), .in2(UJimm), .in3(Uimm), .out(imm), .sel(and_4_out));
endmodule

module alucontrol (
  input  [3:0] Ialu,
  input  [6:0] opcode,
  output [3:0] Balu
);

  wire and_1_out, and_2_out, not_1_out, not_2_out, or_1_out, or_2_out;
  wire [1:0] and_4_out;

  not not_1 (not_1_out, opcode[3]);
  Multiplexer #(.select(2), .width(4), .enable("false")) multiplexer_1 (
    .in0(Ialu), .in1(4'b0000), .in2(4'b0000), .in3(4'b1101), .out(Balu), .sel(and_4_out));
  not not_2 (not_2_out, opcode[2]);
  and and_1 (and_1_out, not_1_out, opcode[5]);
  and and_2 (and_2_out, opcode[5], opcode[2]);
  or or_1 (or_1_out, opcode[3], opcode[4]);
  or or_2 (or_2_out, not_2_out, opcode[4]);
  and and_3 (and_4_out[1], and_2_out, or_1_out);
  and and_4 (and_4_out[0], or_2_out, and_1_out);
endmodule

module Pcsel (
  input  [6:0] opcode,
  input  [2:0] func3,
  input  Breq,
  input  Brlt,
  output Pcsel
);

  wire and_1_out, and_2_out, and_3_out, and_4_out, and_5_out, and_6_out, not_1_out, not_2_out, not_3_out,
       not_4_out, or_2_out;

  not not_1 (not_1_out, Breq);
  not not_2 (not_2_out, opcode[2]);
  not not_3 (not_3_out, func3[0]);
  not not_4 (not_4_out, func3[2]);
  and and_1 (and_1_out, not_1_out, func3[0]);
  and and_2 (and_2_out, opcode[2], opcode[6]);
  and and_3 (and_3_out, opcode[6], not_2_out);
  and and_4 (and_4_out, not_3_out, not_4_out, Breq);
  or or_1 (Pcsel, and_2_out, and_5_out);
  and and_5 (and_5_out, and_3_out, or_2_out);
  and and_6 (and_6_out, func3[2], Brlt);
  or or_2 (or_2_out, and_6_out, and_4_out, and_1_out);
endmodule

module Uimm (
  input  [31:0] instruction1,
  output [31:0] Uimm
);

  wire [31:0] bit_extender_1_out;

  assign bit_extender_1_out = {{12{1'b0}}, instruction1[31:12]};  // Bit_Extender bit_extender_1
  Shifter #(.width(32)) shifter_1 (.in(bit_extender_1_out), .\dist (5'b01100), .out(Uimm));
endmodule

module UJimm (
  input  [31:0] Instruction1,
  output [31:0] UJimm1
);

  assign UJimm1 = {{11{Instruction1[31]}}, {Instruction1[31], Instruction1[19:12], Instruction1[20], Instruction1[30:21], 1'b0}};  // Bit_Extender bit_extender_1
endmodule

module wbsel1 (
  input  [6:0] opcode,
  output [1:0] wbsel
);


  assign wbsel = {opcode[6], opcode[4]};
endmodule

module RegWEn (
  input  [6:0] opcode,
  output regw
);

  wire and_1_out, and_2_out, and_3_out, not_1_out, not_2_out;

  not not_1 (not_1_out, opcode[5]);
  and and_1 (and_1_out, opcode[5], opcode[2]);
  not not_2 (not_2_out, opcode[3]);
  and and_2 (and_2_out, not_2_out, opcode[4]);
  and and_3 (and_3_out, not_2_out, not_1_out);
  or or_1 (regw, and_1_out, and_2_out, and_3_out);
endmodule

module asel1 (
  input  [6:0] opcode,
  output Asel
);

  wire and_1_out, not_1_out, not_2_out;

  not not_1 (not_1_out, opcode[6]);
  not not_2 (not_2_out, opcode[3]);
  and and_1 (and_1_out, opcode[2], not_2_out, opcode[6]);
  nor nor_1 (Asel, and_1_out, not_1_out);
endmodule

module load (
  input  [31:0] address,
  input  [31:0] data,
  input  [2:0] func3,
  output [31:0] dataout
);

  wire [1:0] bit_extender_1_out;
  wire [7:0] multiplexer_1_out;
  wire [15:0] e, f, g, multiplexer_2_out;
  wire [31:0] divider_1_rem, lb, lh;

  Divider #(.width(32)) divider_1 (.a(address), .b(32'h4), .rem(divider_1_rem));  // open: out, upper
  Bit_Extender #(.in_width(32), .out_width(2), .\type ("zero")) bit_extender_1 (
    .in(divider_1_rem), .out(bit_extender_1_out));
  Multiplexer #(.select(2), .width(8), .enable("false")) multiplexer_1 (
    .in0(data[7:0]), .in1(data[15:8]), .in2(data[23:16]), .in3(data[31:24]), .out(multiplexer_1_out),
    .sel(bit_extender_1_out));
  Multiplexer #(.select(2), .width(16), .enable("false")) multiplexer_2 (
    .in0(data[15:0]), .in1(e), .in2(f), .in3(g), .out(multiplexer_2_out), .sel(bit_extender_1_out));
  assign lb = {{24{multiplexer_1_out[7]}}, multiplexer_1_out};  // Bit_Extender bit_extender_2
  Multiplexer #(.select(2), .width(32), .enable("false")) multiplexer_3 (
    .in0(lb), .in1(lh), .in2(data), .out(dataout), .sel(func3[1:0]));  // open: in3
  assign lh = {{16{multiplexer_2_out[15]}}, multiplexer_2_out};  // Bit_Extender bit_extender_3
  assign e = {{8{data[15]}}, data[15:8]};  // Bit_Extender bit_extender_4
  assign f = {{8{data[23]}}, data[23:16]};  // Bit_Extender bit_extender_5
  assign g = {{8{data[31]}}, data[31:24]};  // Bit_Extender bit_extender_6

  // Other names for the same wires on the sheet: a[7:0] = data[7:0]; lower[15:0] = data[15:0]; b[7:0] = data[15:8];
  //   c[7:0] = data[23:16]; upper[15:0] = data[31:16]; d[7:0] = data[31:24]
endmodule
